// Digital circuit iki kapılı araba.dig as structural Verilog
module \iki_kapılı_araba  (
  input  A,
  input  B,
  input  C,
  input  D,
  input  E,
  input  F,
  output Warning_1,
  output Warning_2,
  output Warning_3,
  output Safe
);

  wire and_1_out, not_1_out, or_2_out;

  not not_1 (not_1_out, B);
  or or_1 (Warning_1, A, B);
  xnor xnor_1 (Warning_2, not_1_out, C);
  or or_2 (or_2_out, C, D);
  and and_1 (and_1_out, E, F);
  or or_3 (Warning_3, or_2_out, and_1_out);
  nor nor_1 (Safe, Warning_1, Warning_3);
endmodule
